# Fritzing sketch DistanceSensorSketch (saved by Fritzing 0.9.8b)
breadboards: 1

parts:
  Raspberry_Pi_1 = Raspberry Pi 3 [part_number=RPI-3-V1.2]
  HC-SR04_Sensor_1 = HC-SR04 Ultrasonic Distance Sensor
  R1 = Resistor [tolerance=±5% resistance=2.2k package="1206 [SMD]"]
  R2 = Resistor [tolerance=±5% resistance=1k package="1206 [SMD]"]

nets:
  N1: Raspberry_Pi_1.GIPO4, HC-SR04_Sensor_1.TRIG
  N2: Raspberry_Pi_1.GIPO17, R1.Pin_1, R2.Pin_1
  GND: Raspberry_Pi_1.GND, HC-SR04_Sensor_1.GND
  5V: Raspberry_Pi_1.5V, HC-SR04_Sensor_1.VCC, R2.Pin_0
  N3: HC-SR04_Sensor_1.ECHO, R1.Pin_0
